// Logisim project ARM_V1.circ as structural Verilog
module FA_1 (
  input  A,
  input  B,
  input  Ci,
  output Co,
  output S
);

  wire and_1_out, and_2_out, xor_1_out;

  xor xor_1 (xor_1_out, A, B);
  and and_1 (and_1_out, A, B);
  or or_1 (Co, and_1_out, and_2_out);
  and and_2 (and_2_out, Ci, xor_1_out);
  xor xor_2 (S, xor_1_out, Ci);
endmodule

module FA_4 (
  input  [3:0] A,
  input  [3:0] B,
  input  Cin,
  output Cout,
  output [3:0] Sum
);

  wire fa_1_1_co, fa_1_2_co, fa_1_3_co;

  FA_1 fa_1_1 (.Ci(Cin), .A(A[0]), .B(B[0]), .Co(fa_1_1_co), .S(Sum[0]));
  FA_1 fa_1_2 (.Ci(fa_1_1_co), .A(A[1]), .B(B[1]), .Co(fa_1_2_co), .S(Sum[1]));
  FA_1 fa_1_3 (.Ci(fa_1_2_co), .A(A[2]), .B(B[2]), .Co(fa_1_3_co), .S(Sum[2]));
  FA_1 fa_1_4 (.Ci(fa_1_3_co), .A(A[3]), .B(B[3]), .Co(Cout), .S(Sum[3]));
  Hex_Digit_Display hex_digit_display_1 (.value(Sum), .dp(Cout));
endmodule

module FA_16 (
  input  Cin,
  input  [15:0] A,
  input  [15:0] B,
  output [15:0] Sum,
  output Cout
);

  wire fa_4_1_cout, fa_4_2_cout, fa_4_3_cout;

  FA_4 fa_4_1 (.A(A[3:0]), .B(B[3:0]), .Cin(Cin), .Cout(fa_4_1_cout), .Sum(Sum[3:0]));
  FA_4 fa_4_2 (.A(A[7:4]), .B(B[7:4]), .Cin(fa_4_1_cout), .Cout(fa_4_2_cout), .Sum(Sum[7:4]));
  FA_4 fa_4_3 (.A(A[11:8]), .B(B[11:8]), .Cin(fa_4_2_cout), .Cout(fa_4_3_cout), .Sum(Sum[11:8]));
  FA_4 fa_4_4 (.A(A[15:12]), .B(B[15:12]), .Cin(fa_4_3_cout), .Cout(Cout), .Sum(Sum[15:12]));
endmodule

module FA_32 (
  input  [31:0] A,
  input  cin,
  input  [31:0] B,
  output [31:0] Sum32,
  output cout
);

  wire fa_16_1_cout;

  FA_16 fa_16_1 (.Cin(cin), .A(A[15:0]), .B(B[15:0]), .Cout(fa_16_1_cout), .Sum(Sum32[15:0]));
  FA_16 fa_16_2 (.Cin(fa_16_1_cout), .A(A[31:16]), .B(B[31:16]), .Cout(cout), .Sum(Sum32[31:16]));
endmodule

module ULA (
  input  cin,
  input  [31:0] A,
  input  [31:0] B,
  input  [4:0] shift_rot,
  input  [3:0] opCode,
  input  [1:0] opCode_2,
  output [31:0] B_2,
  output carry
);

  wire adc_sbc_1_cout, cmp_cmn_1_cout, fa_32_1_cout, not_2_out;
  wire [31:0] adc_sbc_1_result, and_2_out, and_out, cmp_cmn_1_result, fa_32_1_sum32, multiplier_1_out,
       not_1_out, or_out, shifter_1_out, shifter_2_out, shifter_3_out, shifter_4_out, xor_out;

  assign not_1_out = ~B;  // NOT_Gate not_1, 32 bits wide
  CMP_CMN cmp_cmn_1 (.A(A), .B(B), .Cin(cin), .Cout(cmp_cmn_1_cout), .Result(cmp_cmn_1_result));
  not not_2 (not_2_out, cin);
  assign and_out = A & B;  // AND_Gate and, 32 bits wide
  assign xor_out = B ^ A;  // XOR_Gate xor, 32 bits wide
  ADC_SBC adc_sbc_1 (.A(A), .B(B), .Cin(cin), .Cout(adc_sbc_1_cout), .ADC_SBC_b21cb356(cin), .Result(adc_sbc_1_result));
  Shifter #(.width(32)) shifter_1 (.in(B), .\dist (shift_rot), .out(shifter_1_out));
  Shifter #(.width(32), .shift("lr")) shifter_2 (.in(B), .\dist (shift_rot), .out(shifter_2_out));
  Shifter #(.width(32), .shift("ar")) shifter_3 (.in(B), .\dist (shift_rot), .out(shifter_3_out));
  Multiplier #(.width(32)) multiplier_1 (.a(A), .b(B), .out(multiplier_1_out), .cin({32{1'b1}}));  // open: cout
  FA_32 fa_32_1 (.A({32{1'b1}}), .B(not_1_out), .cin(not_2_out), .cout(fa_32_1_cout), .Sum32(fa_32_1_sum32));
  assign or_out = B | A;  // OR_Gate or, 32 bits wide
  Shifter #(.width(32), .shift("rl")) shifter_4 (.in(not_1_out), .\dist (shift_rot), .out(shifter_4_out));
  Multiplexer #(.select(2)) multiplexer_1 (
    .in0(fa_32_1_cout), .in1(adc_sbc_1_cout), .in2(cmp_cmn_1_cout), .out(carry), .sel(opCode_2));  // open: in3, en
  assign and_2_out = A & not_1_out;  // AND_Gate and_2, 32 bits wide
  Multiplexer #(.select(4), .width(32)) multiplexer_2 (
    .in0(and_out), .in1(xor_out), .in2(shifter_1_out), .in3(shifter_2_out), .in4(shifter_3_out),
    .in5(adc_sbc_1_result), .in6(adc_sbc_1_result), .in7(shifter_4_out), .in8(and_out), .in9(fa_32_1_sum32),
    .in10(cmp_cmn_1_result), .in11(cmp_cmn_1_result), .in12(or_out), .in13(multiplier_1_out),
    .in14(and_2_out), .in15(not_1_out), .out(B_2), .sel(opCode));  // open: en

  // Notes on the sheet:
  //   Sub
endmodule

module CMP_CMN (
  input  Cin,
  input  [31:0] A,
  input  [31:0] B,
  output [31:0] Result,
  output Cout
);

  wire [31:0] multiplexer_1_out, not_1_out;

  assign not_1_out = ~B;  // NOT_Gate not_1, 32 bits wide
  Multiplexer #(.width(32)) multiplexer_1 (.in0(not_1_out), .in1(B), .out(multiplexer_1_out), .sel(Cin));  // open: en
  FA_32 fa_32_1 (.A(A), .B(multiplexer_1_out), .cin(Cin), .cout(Cout), .Sum32(Result));
endmodule

module ADC_SBC (
  input  Cin,
  input  [31:0] A,
  input  ADC_SBC_b21cb356,
  input  [31:0] B,
  output [31:0] Result,
  output Cout
);

  wire multiplexer_2_out, not_2_out;
  wire [31:0] multiplexer_1_out, not_1_out;

  assign not_1_out = ~B;  // NOT_Gate not_1, 32 bits wide
  Multiplexer #(.width(32)) multiplexer_1 (.in0(not_1_out), .in1(B), .out(multiplexer_1_out), .sel(Cin));  // open: en
  not not_2 (not_2_out, Cin);
  Multiplexer multiplexer_2 (.in0(Cin), .in1(not_2_out), .out(multiplexer_2_out), .sel(ADC_SBC_b21cb356));  // open: en
  FA_32 fa_32_1 (.A(A), .B(multiplexer_1_out), .cin(multiplexer_2_out), .cout(Cout), .Sum32(Result));
endmodule

module ULA_simple (
  input  [31:0] A,
  input  [31:0] B,
  input  [4:0] shift,
  input  [3:0] opCode,
  input  cin,
  input  ADC_SBC,
  input  [1:0] opCode_2,
  output [31:0] res,
  output N,
  output C,
  output Z,
  output O
);

  wire and_3_out, and_4_out, and_5_out, and_6_out, carry_ADC_SBC, carry_CMP_CMN, carry_RSB, not_1_out,
       not_2_out, not_3_out, or_3_out;
  wire [31:0] ADC_SBC_t, AND, ASR, BIC, CMP_CMN, EOR, LSL, LSR, MUL, MVN, NOT_B_out, ORR, ROR, RSB, XOR;

  assign NOT_B_out = ~B;  // NOT_Gate NOT_B, 32 bits wide
  Shifter #(.width(32)) shifter_1 (.in(B), .\dist (shift), .out(LSL));
  Shifter #(.width(32), .shift("lr")) shifter_2 (.in(B), .\dist (shift), .out(LSR));
  Shifter #(.width(32), .shift("ar")) shifter_3 (.in(B), .\dist (shift), .out(ASR));
  Shifter #(.width(32), .shift("rl")) shifter_4 (.in(B), .\dist (shift), .out(ROR));
  assign AND = A & B;  // AND_Gate and, 32 bits wide
  assign XOR = A ^ B;  // XOR_Gate xor, 32 bits wide
  assign ORR = A | B;  // OR_Gate or_1, 32 bits wide
  assign BIC = A & NOT_B_out;  // AND_Gate and_2, 32 bits wide
  and and_3 (and_3_out, A[31], B[31]);
  not not_1 (not_1_out, N);
  not not_2 (not_2_out, A[31]);
  and and_4 (and_4_out, not_2_out, not_3_out);
  not not_3 (not_3_out, B[31]);
  Multiplexer #(.select(2)) multiplexer_1 (
    .in0(carry_ADC_SBC), .in1(carry_RSB), .in2(carry_CMP_CMN), .out(C), .sel(opCode_2));  // open: in3, en
  and and_5 (and_5_out, and_3_out, not_1_out);
  and and_6 (and_6_out, and_4_out, N);
  or or_2 (O, and_5_out, and_6_out);
  ADC_SBC adc_sbc_1 (.A(A), .B(B), .Cin(cin), .Cout(carry_ADC_SBC), .ADC_SBC_b21cb356(ADC_SBC), .Result(ADC_SBC_t));
  CMP_CMN cmp_cmn_1 (.A({32{1'b1}}), .B(B), .Cin(cin), .Cout(carry_RSB), .Result(RSB));
  CMP_CMN cmp_cmn_2 (.A(A), .B(B), .Cin(cin), .Cout(carry_CMP_CMN), .Result(CMP_CMN));
  Multiplier #(.width(32)) multiplier_1 (.a(A), .b(B), .out(MUL));  // open: cin, cout
  or or_3 (or_3_out, res[0], res[1], res[2], res[3], res[4], res[5], res[6], res[7], res[8], res[9], res[10], res[11], res[12], res[13], res[14], res[15], res[16], res[17], res[18], res[19], res[20], res[21], res[22], res[23], res[24], res[25], res[26], res[27], res[28], res[29], res[30]);
  Multiplexer #(.select(4), .width(32)) multiplexer_2 (
    .in0(AND), .in1(EOR), .in2(LSL), .in3(LSR), .in4(ASR), .in5(ADC_SBC_t), .in6(ADC_SBC_t), .in7(ROR),
    .in8(AND), .in9(RSB), .in10(CMP_CMN), .in11(CMP_CMN), .in12(ORR), .in13(MUL), .in14(BIC), .in15(MVN),
    .out({N, res[30:0]}), .sel(opCode));  // open: en
  not not_4 (Z, or_3_out);

  assign res[31] = N;

  // Other names for the same wires on the sheet: inA[31:0] = A; inB[31:0] = B
endmodule
