// Logisim project ARM_V2.circ as structural Verilog
module FA_1 (
  input  A,
  input  B,
  input  Ci,
  output Co,
  output S
);

  wire and_1_out, and_2_out, xor_1_out;

  xor xor_1 (xor_1_out, A, B);
  and and_1 (and_1_out, A, B);
  or or_1 (Co, and_1_out, and_2_out);
  and and_2 (and_2_out, Ci, xor_1_out);
  xor xor_2 (S, xor_1_out, Ci);
endmodule

module FA_4 (
  input  [3:0] A,
  input  [3:0] B,
  input  Cin,
  output Cout,
  output [3:0] Sum
);

  wire FA_1_2_p4, FA_1_2_p5, FA_1_3_p4, FA_1_4_p4, FA_1_4_p5;

  // FA_1 FA_1_3: pin names not known; wires that end beside it: B[0], Cin, A[0], FA_1_3_p4, Sum[0], A[1], B[1]
  // FA_1 FA_1_2: pin names not known; wires that end beside it: B[1], FA_1_3_p4, A[1], FA_1_2_p4, FA_1_2_p5, Sum[1], A[2], B[2]
  // FA_1 FA_1_4: pin names not known; wires that end beside it: B[2], FA_1_2_p4, A[2], FA_1_4_p4, FA_1_4_p5, Sum[2], A[3], B[3]
  // FA_1 FA_1_1: pin names not known; wires that end beside it: B[3], FA_1_4_p4, A[3], Cout, Sum[3]
endmodule

module FA_16 (
  input  Cin,
  input  [15:0] A,
  input  [15:0] B,
  output [15:0] Sum,
  output Cout
);

  wire FA_4_2_p1, FA_4_3_p1, FA_4_4_p1;

  // FA_4 FA_4_2: pin names not known; wires that end beside it: FA_4_2_p1, Sum[3:0]
  // FA_4 FA_4_3: pin names not known; wires that end beside it: FA_4_3_p1, Sum[7:4]
  // FA_4 FA_4_4: pin names not known; wires that end beside it: FA_4_4_p1, Sum[11:8]
  // FA_4 FA_4_1: pin names not known; wires that end beside it: Cout, Sum[15:12]
endmodule

module FA_32 (
  input  [31:0] A,
  input  cin,
  input  [31:0] B,
  output [31:0] Sum32,
  output cout
);

  wire FA_16_1_p2;

  // FA_16 FA_16_1: pin names not known; wires that end beside it: Sum32[15:0], FA_16_1_p2
  // FA_16 FA_16_2: pin names not known; wires that end beside it: Sum32[31:16], cout
endmodule

module ULA (
  input  cin,
  input  [31:0] A,
  input  [31:0] B,
  input  [4:0] shift_rot,
  input  [3:0] opCode,
  input  [1:0] opCode_2,
  output [31:0] B_2,
  output carry
);

  wire adc_sbc_1_cout, fa_32_1_cout, not_2_out, undriven;
  wire [31:0] adc_sbc_1_result, and_2_out, and_out, cmp_cmn_1_result, fa_32_1_sum32, multiplier_1_out,
       not_1_out, or_out, shifter_1_out, shifter_2_out, shifter_3_out, shifter_4_out, xor_out;

  assign not_1_out = ~B;  // NOT_Gate not_1, 32 bits wide
  CMP_CMN cmp_cmn_1 (.A(A), .B(B), .Cin(cin), .Result(cmp_cmn_1_result));  // open: cout
  not not_2 (not_2_out, cin);
  assign and_out = A & B;  // AND_Gate and, 32 bits wide
  assign xor_out = B ^ A;  // XOR_Gate xor, 32 bits wide
  ADC_SBC adc_sbc_1 (.A(A), .B(B), .Cin(cin), .Cout(adc_sbc_1_cout), .ADC_SBC_b21cb356(cin), .Result(adc_sbc_1_result));
  Shifter #(.width(32)) shifter_1 (.in(B), .\dist (shift_rot), .out(shifter_1_out));
  Shifter #(.width(32), .shift("lr")) shifter_2 (.in(B), .\dist (shift_rot), .out(shifter_2_out));
  Shifter #(.width(32), .shift("ar")) shifter_3 (.in(B), .\dist (shift_rot), .out(shifter_3_out));
  Multiplier #(.width(32)) multiplier_1 (.a(A), .b(B), .out(multiplier_1_out), .cin({32{1'b1}}));  // open: cout
  FA_32 fa_32_1 (.A({32{1'b1}}), .B(not_1_out), .cin(not_2_out), .cout(fa_32_1_cout), .Sum32(fa_32_1_sum32));
  assign or_out = B | A;  // OR_Gate or, 32 bits wide
  Shifter #(.width(32), .shift("rl")) shifter_4 (.in(not_1_out), .\dist (shift_rot), .out(shifter_4_out));
  Multiplexer #(.select(2)) multiplexer_1 (
    .in0(fa_32_1_cout), .in1(adc_sbc_1_cout), .in2(undriven), .out(carry), .sel(opCode_2));  // open: in3, en
  assign and_2_out = A & not_1_out;  // AND_Gate and_2, 32 bits wide
  Multiplexer #(.select(4), .width(32)) multiplexer_2 (
    .in0(and_out), .in1(xor_out), .in2(shifter_1_out), .in3(shifter_2_out), .in4(shifter_3_out),
    .in5(adc_sbc_1_result), .in6(adc_sbc_1_result), .in7(shifter_4_out), .in8(and_out), .in9(fa_32_1_sum32),
    .in10(cmp_cmn_1_result), .in11(cmp_cmn_1_result), .in12(or_out), .in13(multiplier_1_out),
    .in14(and_2_out), .in15(not_1_out), .out(B_2), .sel(opCode));  // open: en

  // Notes on the sheet:
  //   Sub
endmodule

module CMP_CMN (
  input  Cin,
  input  [31:0] A,
  input  [31:0] B,
  output [31:0] Result,
  output cout
);

  wire [31:0] multiplexer_1_out, not_1_out;

  assign not_1_out = ~B;  // NOT_Gate not_1, 32 bits wide
  Multiplexer #(.width(32)) multiplexer_1 (.in0(not_1_out), .in1(B), .out(multiplexer_1_out), .sel(Cin));  // open: en
  // FA_32 FA_32_1: pin names not known; wires that end beside it: Result, cout
endmodule

module ADC_SBC (
  input  Cin,
  input  [31:0] A,
  input  ADC_SBC_b21cb356,
  input  [31:0] B,
  output [31:0] Result,
  output Cout
);

  wire multiplexer_2_out, not_2_out;
  wire [31:0] multiplexer_1_out, not_1_out;

  assign not_1_out = ~B;  // NOT_Gate not_1, 32 bits wide
  Multiplexer #(.width(32)) multiplexer_1 (.in0(not_1_out), .in1(B), .out(multiplexer_1_out), .sel(Cin), .en(Cin));
  not not_2 (not_2_out, Cin);
  Multiplexer multiplexer_2 (
    .in0(Cin), .in1(not_2_out), .out(multiplexer_2_out), .sel(ADC_SBC_b21cb356), .en(not_2_out));
  // FA_32 FA_32_1: pin names not known; wires that end beside it: Result, Cout
endmodule

module testALU (
  input  [6:0] Input_bus_1,
  input  [3:0] Input_bus_3,
  input  [7:0] Input_bus_2,
  output [7:0] Output_bus_1,
  output Output_1
);

  wire ULA_simple_1_p2, ULA_simple_1_p3;
  wire [31:8] ULA_simple_1_p1;

  // ULA_simple ULA_simple_1: pin names not known; wires that end beside it: {ULA_simple_1_p1, Output_bus_1}, ULA_simple_1_p2, ULA_simple_1_p3
  or or_1 (Output_1, ULA_simple_1_p2, ULA_simple_1_p3);
endmodule

module ULA_simple (
  input  [31:0] A,
  input  [31:0] B,
  input  [4:0] shift,
  input  [3:0] opCode2,
  input  cin,
  input  ADC_SBC1,
  output [31:0] res,
  output C,
  output N,
  output Z,
  output O
);

  wire and_3_out, and_4_out, and_5_out, and_6_out, carry_ADC_SBC, carry_CMP_CMN, carry_RSB, not_1_out,
       not_2_out, not_3_out, or_5_out;
  wire [1:0] comparator_1_eq;
  wire [3:0] or_2_out, or_3_out;
  wire [31:0] ADC_SBC, ADC_SBC2, AND, ASR, BIC, CMP_CMN, EOR, LSL, LSR, MUL, MVN, NOT_B_out, ORR, ROR, RSB,
       XOR;

  assign NOT_B_out = ~B;  // NOT_Gate NOT_B, 32 bits wide
  Shifter #(.width(32)) shifter_1 (.in(B), .\dist (shift), .out(LSL));
  Shifter #(.width(32), .shift("lr")) shifter_2 (.in(B), .\dist (shift), .out(LSR));
  Shifter #(.width(32), .shift("ar")) shifter_3 (.in(B), .\dist (shift), .out(ASR));
  Shifter #(.width(32), .shift("rl")) shifter_4 (.in(B), .\dist (shift), .out(ROR));
  assign AND = A & B;  // AND_Gate and, 32 bits wide
  assign XOR = A ^ B;  // XOR_Gate xor, 32 bits wide
  assign ORR = A | B;  // OR_Gate or_1, 32 bits wide
  assign BIC = A & NOT_B_out;  // AND_Gate and_2, 32 bits wide
  assign or_2_out = 4'b0101 | 4'b0110;  // OR_Gate or_2, 4 bits wide
  assign or_3_out = 4'b1010 | 4'b1011;  // OR_Gate or_3, 4 bits wide
  not not_1 (not_1_out, N);
  not not_2 (not_2_out, A[31]);
  not not_3 (not_3_out, B[31]);
  Comparator #(.width(4)) comparator_1 (.a(or_2_out), .b(opCode2), .eq(comparator_1_eq[0]));  // open: gt, lt
  Comparator #(.width(4)) comparator_2 (.a(opCode2), .b(or_3_out), .eq(comparator_1_eq[1]));  // open: gt, lt
  and and_3 (and_3_out, A[31], B[31]);
  and and_4 (and_4_out, and_3_out, not_1_out);
  and and_5 (and_5_out, not_2_out, not_3_out);
  and and_6 (and_6_out, and_5_out, N);
  Multiplexer #(.select(2)) multiplexer_1 (
    .in0(carry_ADC_SBC), .in1(carry_RSB), .in2(carry_CMP_CMN), .out(C), .sel(comparator_1_eq));  // open: in3, en
  or or_4 (O, and_4_out, and_6_out);
  or or_5 (or_5_out, res[0], res[1], res[2], res[3], res[4], res[5], res[6], res[7], res[8], res[9], res[10], res[11], res[12], res[13], res[14], res[15], res[16], res[17], res[18], res[19], res[20], res[21], res[22], res[23], res[24], res[25], res[26], res[27], res[28], res[29], res[30]);
  // ADC_SBC ADC_SBC_1: pin names not known; wires that end beside it: ADC_SBC2, carry_ADC_SBC
  not not_4 (Z, or_5_out);
  // CMP_CMN CMP_CMN_2: pin names not known; wires that end beside it: RSB, carry_RSB
  // CMP_CMN CMP_CMN_1: pin names not known; wires that end beside it: CMP_CMN, carry_CMP_CMN
  Multiplier #(.width(32)) multiplier_1 (.a(A), .b(B), .out(MUL));  // open: cin, cout
  Multiplexer #(.select(4), .width(32)) multiplexer_2 (
    .in0(AND), .in1(EOR), .in2(LSL), .in3(LSR), .in4(ASR), .in5(ADC_SBC), .in6(ADC_SBC), .in7(ROR),
    .in8(AND), .in9(RSB), .in10(CMP_CMN), .in11(CMP_CMN), .in12(ORR), .in13(MUL), .in14(BIC), .in15(MVN),
    .out({N, res[30:0]}), .sel(opCode2), .en(1'b0));

  assign res[31] = N;

  // Other names for the same wires on the sheet: inA[31:0] = A; inB[31:0] = B; opcod[3:0] = opCode2
endmodule

module test_alu (
  input  Input_1,
  input  Input_3,
  input  Input_4,
  input  Input_6,
  input  Input_8,
  input  Input_9,
  input  Input_7,
  input  [3:0] Input_bus_1,
  input  [7:0] Input_bus_2,
  output [7:0] Output_bus_1,
  output Output_1
);

  wire ULA_simple_1_p2, ULA_simple_1_p3;
  wire [31:8] ULA_simple_1_p1;

  // ULA_simple ULA_simple_1: pin names not known; wires that end beside it: {ULA_simple_1_p1, Output_bus_1}, ULA_simple_1_p2, ULA_simple_1_p3
  and and_1 (Output_1, ULA_simple_1_p2, ULA_simple_1_p3);
endmodule

module test_FA4 (
  input  [3:0] Input_bus_2,
  input  [3:0] Input_bus_1,
  input  Input_1,
  output Output_1,
  output [3:0] Output_bus_1
);

  // FA_4 FA_4_1: pin names not known; wires that end beside it: Output_1, Output_bus_1
endmodule

module demo (
  input  [6:0] Input_bus_1,
  input  [6:0] Input_bus_2,
  input  Input_1,
  output [7:0] Output_bus_1,
  output [7:0] Output_bus_2,
  output N,
  output C,
  output Z,
  output O
);

  wire [31:16] ULA_simple_1_p1;

  // ULA_simple ULA_simple_1: pin names not known; wires that end beside it: {ULA_simple_1_p1, Output_bus_2, Output_bus_1}, N, C, Z
endmodule

module tryADD (
  input  [6:0] Input_bus_1,
  input  [6:0] Input_bus_2,
  input  Input_1,
  output [7:0] Output_bus_1,
  output [7:0] Output_bus_2,
  output N,
  output C,
  output Z,
  output O
);

  wire [31:16] ULA_simple_1_p1;

  // ULA_simple ULA_simple_1: pin names not known; wires that end beside it: {ULA_simple_1_p1, Output_bus_2, Output_bus_1}, N, C, Z
endmodule
