// Logisim project Opcode.circ as structural Verilog: 1 circuit, main circuit main
module main (
  input  c5,
  input  c4,
  input  c3,
  input  c2,
  input  c1,
  input  c0,
  output DataP,
  output Shift,
  output LoadStore,
  output Branch,
  output NOP
);

  wire and_3_out, and_4_out, and_5_out, and_7_out, and_8_out, and_9_out, and_10_out, and_11_out, and_12_out,
       and_13_out, and_14_out, not_1_out, not_2_out, not_3_out, not_4_out, not_5_out, not_6_out, not_7_out,
       not_8_out, not_9_out, not_10_out, not_11_out, not_12_out, not_13_out, not_14_out, not_15_out,
       not_16_out, not_17_out, not_18_out, not_19_out, not_20_out, not_21_out, not_22_out, not_23_out,
       not_24_out, not_25_out, not_26_out, not_27_out, not_28_out, not_29_out, not_30_out, not_31_out,
       not_32_out;

  not not_1 (not_1_out, c5);
  not not_2 (not_2_out, c3);
  not not_3 (not_3_out, c2);
  not not_4 (not_4_out, c1);
  not not_5 (not_5_out, c5);
  not not_6 (not_6_out, c4);
  not not_7 (not_7_out, c5);
  not not_8 (not_8_out, c3);
  not not_9 (not_9_out, c5);
  not not_10 (not_10_out, c4);
  not not_11 (not_11_out, c3);
  not not_12 (not_12_out, c3);
  not not_13 (not_13_out, c5);
  not not_14 (not_14_out, c3);
  not not_15 (not_15_out, c2);
  not not_16 (not_16_out, c1);
  not not_17 (not_17_out, c5);
  not not_18 (not_18_out, c3);
  not not_19 (not_19_out, c2);
  not not_20 (not_20_out, c4);
  not not_21 (not_21_out, c2);
  not not_22 (not_22_out, c1);
  not not_23 (not_23_out, c4);
  not not_24 (not_24_out, c2);
  not not_25 (not_25_out, c4);
  not not_26 (not_26_out, c3);
  not not_27 (not_27_out, c2);
  not not_28 (not_28_out, c1);
  not not_29 (not_29_out, c3);
  not not_30 (not_30_out, c2);
  not not_31 (not_31_out, c2);
  not not_32 (not_32_out, c1);
  and and_1 (DataP, not_1_out, c4, not_2_out, not_3_out, not_4_out);
  and and_2 (Shift, not_5_out, not_6_out);
  and and_3 (and_3_out, not_7_out, c4, not_8_out, c2);
  and and_4 (and_4_out, not_9_out, c4, c3);
  and and_5 (and_5_out, c5, not_10_out, not_11_out);
  and and_6 (Branch, c5, c4, not_12_out, c2);
  and and_7 (and_7_out, not_13_out, c4, not_14_out, not_15_out, not_16_out, c0);
  and and_8 (and_8_out, not_17_out, c4, not_18_out, not_19_out, c1);
  and and_9 (and_9_out, c5, not_20_out, c3, not_21_out, not_22_out);
  and and_10 (and_10_out, c5, not_23_out, c3, not_24_out, c1);
  and and_11 (and_11_out, c5, not_25_out, c3, c2);
  and and_12 (and_12_out, c5, c4, not_26_out, not_27_out, not_28_out);
  and and_13 (and_13_out, c5, c4, not_29_out, not_30_out, c1);
  and and_14 (and_14_out, c5, c4, c3, not_31_out, not_32_out);
  or or_1 (LoadStore, and_3_out, and_4_out, and_5_out);
  or or_2 (NOP, and_7_out, and_8_out, and_9_out, and_10_out, and_11_out, and_12_out, and_13_out, and_14_out);
endmodule
