// Logisim project BancFiltre.circ as structural Verilog: 2 circuits, main circuit BR32
module BR32 (
  input  [31:0] E,
  input  Clk,
  input  LectEcr,
  input  [3:0] Rm,
  input  [3:0] Rn,
  input  [3:0] Rd,
  output [31:0] A,
  output [31:0] B
);

  wire WE0, WE1, WE2, WE3, WE4, WE5, WE6, WE7, WE8, WE9, WE10, WE11, WE12, WE13, WE14, WE15;
  wire [31:0] R0, R1, R2, R3, R4, R5, R6, R7, R8, R9, R10, R11, R12, R13, R14, R15;

  Register #(.width(32)) register_1 (.D(E), .en(WE0), .clk(Clk), .Q(R0));  // open: clr
  Register #(.width(32)) register_2 (.D(E), .en(WE8), .clk(Clk), .Q(R8));  // open: clr
  Register #(.width(32)) register_3 (.D(E), .en(WE1), .clk(Clk), .Q(R1));  // open: clr
  Register #(.width(32)) register_4 (.D(E), .en(WE9), .clk(Clk), .Q(R9));  // open: clr
  Multiplexer #(.select(4), .width(32), .enable("false")) multiplexer_1 (
    .in0(R0), .in1(R1), .in2(R2), .in3(R3), .in4(R4), .in5(R5), .in6(R6), .in7(R7), .in8(R8), .in9(R9),
    .in10(R10), .in11(R11), .in12(R12), .in13(R13), .in14(R14), .in15(R15), .out(A), .sel(Rn));
  Register #(.width(32)) register_5 (.D(E), .en(WE2), .clk(Clk), .Q(R2));  // open: clr
  Register #(.width(32)) register_6 (.D(E), .en(WE10), .clk(Clk), .Q(R10));  // open: clr
  Register #(.width(32)) register_7 (.D(E), .en(WE3), .clk(Clk), .Q(R3));  // open: clr
  Register #(.width(32)) register_8 (.D(E), .en(WE11), .clk(Clk), .Q(R11));  // open: clr
  Decoder #(.select(4)) decoder_1 (
    .out0(WE0), .out1(WE1), .out2(WE2), .out3(WE3), .out4(WE4), .out5(WE5), .out6(WE6), .out7(WE7),
    .out8(WE8), .out9(WE9), .out10(WE10), .out11(WE11), .out12(WE12), .out13(WE13), .out14(WE14),
    .out15(WE15), .sel(Rd), .en(LectEcr));
  Register #(.width(32)) register_9 (.D(E), .en(WE4), .clk(Clk), .Q(R4));  // open: clr
  Register #(.width(32)) register_10 (.D(E), .en(WE12), .clk(Clk), .Q(R12));  // open: clr
  Register #(.width(32)) register_11 (.D(E), .en(WE5), .clk(Clk), .Q(R5));  // open: clr
  Register #(.width(32)) register_12 (.D(E), .en(WE13), .clk(Clk), .Q(R13));  // open: clr
  Register #(.width(32)) register_13 (.D(E), .en(WE6), .clk(Clk), .Q(R6));  // open: clr
  Register #(.width(32)) register_14 (.D(E), .en(WE14), .clk(Clk), .Q(R14));  // open: clr
  Multiplexer #(.select(4), .width(32), .enable("false")) multiplexer_2 (
    .in0(R0), .in1(R1), .in2(R2), .in3(R3), .in4(R4), .in5(R5), .in6(R6), .in7(R7), .in8(R8), .in9(R9),
    .in10(R10), .in11(R11), .in12(R12), .in13(R13), .in14(R14), .in15(R15), .out(B), .sel(Rm));
  Register #(.width(32)) register_15 (.D(E), .en(WE7), .clk(Clk), .Q(R7));  // open: clr
  Register #(.width(32)) register_16 (.D(E), .en(WE15), .clk(Clk), .Q(R15));  // open: clr

  // Notes on the sheet:
  //   Entrées
  //   Selection A et B
  //   Banc de Registres
  //   Décodeur
  //   Sorties
endmodule

module RM (
  input  LectEcr,
  input  [3:0] Rn,
  input  [3:0] Rm,
  input  [3:0] Rd,
  output [31:0] Sortie
);

  wire Clk, not_1_out;
  wire [7:0] bitselector_1_out, DA_q;
  wire [31:0] br32_1_a, multiplexer_1_out, RAM;

  Clock u_Clk (.out(Clk));
  Multiplexer #(.width(32), .enable("false")) multiplexer_1 (
    .in0(Sortie), .in1(RAM), .out(multiplexer_1_out), .sel(LectEcr));
  BR32 br32_1 (.Rm(Rn), .E(multiplexer_1_out), .Rd(Rd), .LectEcr(LectEcr), .Rn(Rm), .A(br32_1_a), .B(RAM), .Clk(Clk));
  assign Sortie = br32_1_a & RAM;  // AND_Gate and_1, 32 bits wide
  Register DA (.D(bitselector_1_out), .en(LectEcr), .clk(Clk), .Q(DA_q));  // open: clr
  BitSelector #(.width(32), .group(8)) bitselector_1 (.in(Sortie), .out(bitselector_1_out));  // open: sel
  RAM #(.dataWidth(32)) ram_1 (.addr(DA_q), .we(LectEcr), .oe(not_1_out), .clk(Clk), .data(RAM));
  not not_1 (not_1_out, LectEcr);
endmodule
