// Logisim project BancRegistres.circ as structural Verilog: 4 circuits, main circuit BR32
module BR32 (
  input  [31:0] E,
  input  Clk,
  input  LectEcr,
  input  [2:0] Rm,
  input  [2:0] Rn,
  input  [2:0] Rd,
  output [31:0] A,
  output [31:0] B
);

  wire WE0, WE1, WE2, WE3, WE4, WE5, WE6, WE7;
  wire [31:0] R0, R1, R2, R3, R4, R5, R6, R7;

  Multiplexer #(.select(3), .width(32), .enable("false")) multiplexer_1 (
    .in0(R0), .in1(R1), .in2(R2), .in3(R3), .in4(R4), .in5(R5), .in6(R6), .in7(R7), .out(A), .sel(Rn));
  Multiplexer #(.select(3), .width(32), .enable("false")) multiplexer_2 (
    .in0(R0), .in1(R1), .in2(R2), .in3(R3), .in4(R4), .in5(R5), .in6(R6), .in7(R7), .out(B), .sel(Rm));
  Register #(.width(32)) register_1 (.D(E), .en(WE0), .clk(Clk), .Q(R0));  // open: clr
  Decoder #(.select(3)) decoder_1 (
    .out0(WE0), .out1(WE1), .out2(WE2), .out3(WE3), .out4(WE4), .out5(WE5), .out6(WE6), .out7(WE7), .sel(Rd),
    .en(LectEcr));
  Register #(.width(32)) register_2 (.D(E), .en(WE1), .clk(Clk), .Q(R1));  // open: clr
  Register #(.width(32)) register_3 (.D(E), .en(WE2), .clk(Clk), .Q(R2));  // open: clr
  Register #(.width(32)) register_4 (.D(E), .en(WE3), .clk(Clk), .Q(R3));  // open: clr
  Register #(.width(32)) register_5 (.D(E), .en(WE4), .clk(Clk), .Q(R4));  // open: clr
  Register #(.width(32)) register_6 (.D(E), .en(WE5), .clk(Clk), .Q(R5));  // open: clr
  Register #(.width(32)) register_7 (.D(E), .en(WE6), .clk(Clk), .Q(R6));  // open: clr
  Register #(.width(32)) register_8 (.D(E), .en(WE7), .clk(Clk), .Q(R7));  // open: clr

  // Notes on the sheet:
  //   Entrées
  //   Inputs
  //   Selection A et B
  //   A clock to run registers
  //   Load / Store
  //   From Controleur
  //   Décodeur
  //   Banc de Registres
  //   Rn says : A takes value from this register (ex : if Rn = 001 , A = value of register identified by 001 (R1)
  //   Rm says : B takes value from this register
  //   We choose with the value of Rd (From Controleur) 
  //   in wich register we store the input E
  //   Registers (8*32bits)
  //   Sorties
  //   Outputs
endmodule

module RM (
  input  Sel,
  input  LectEcr,
  input  [2:0] Rn,
  input  [2:0] Rm,
  input  [2:0] Rd,
  input  [3:0] codeop,
  input  [4:0] Shift,
  input  Cin,
  output [31:0] Sortie,
  output [1:0] Flags
);

  wire Clk, not_1_out, Z;
  wire [7:0] bitselector_1_out, DA_q;
  wire [31:0] br32_1_a, br32_1_b, multiplexer_1_out, RAM;

  Clock u_Clk (.out(Clk));
  Multiplexer #(.width(32), .enable("false")) multiplexer_1 (
    .in0(Sortie), .in1(RAM), .out(multiplexer_1_out), .sel(Sel));
  BR32 br32_1 (
    .E(multiplexer_1_out), .Rd(Rd), .B(br32_1_b), .A(br32_1_a), .Rm(Rn), .LectEcr(LectEcr), .Rn(Rm), .Clk(Clk));
  assign RAM = LectEcr ? br32_1_b : 32'bz;  // Controlled_Buffer controlled_buffer_1
  // ULA_simple ula_simple_1: pin names not known; wires that end beside it: Sortie, Flags[1], Flags[0], Z
  BitSelector #(.width(32), .group(8)) bitselector_1 (.in(Sortie), .out(bitselector_1_out));  // open: sel
  Register DA (.D(bitselector_1_out), .en(LectEcr), .clk(Clk), .Q(DA_q));  // open: clr
  RAM #(.dataWidth(32)) ram_1 (.addr(DA_q), .we(LectEcr), .oe(not_1_out), .clk(Clk), .data(RAM));
  not not_1 (not_1_out, LectEcr);

  // Other names for the same wires on the sheet: N = Flags[0]; C = Flags[1]

  // Notes on the sheet:
  //   Flags (outputs) from the ALU
  //   Selection
  //   Load / Store
  //   Inputs from Controleur
  //   ALU
  //   RAM (Memory) to store B if LectEcr is 1 at the adress corresponding of the 8 first bits of the output of the ALU
endmodule

module TestRM (
  input  Sel,
  input  LectEcr,
  input  [2:0] Rn,
  input  [2:0] Rm,
  input  [2:0] Rd,
  input  [3:0] Codeop,
  input  [4:0] shift,
  input  Cin,
  input  ADC_SBC1,
  output [31:0] S,
  output [1:0] flags
);

  // RM rm_1: pin names not known; wires that end beside it: S, flags
endmodule

module testBR (
  input  [6:0] in_1,
  input  [2:0] in_2,
  input  [2:0] in_3,
  input  [2:0] in_4,
  output [6:0] out_5,
  output [6:0] out_6
);

  wire undriven;
  wire [7:0] br32_1_a_2, br32_1_a_3, br32_1_a_4;
  wire [7:7] br32_1_a;
  wire [31:7] br32_1_b;
  wire [31:8] undriven_2;

  BR32 br32_1 (
    .E({undriven_2, 1'b0, in_1}), .Rd(in_4), .B({br32_1_b, out_5}),
    .A({br32_1_a_4, br32_1_a_3, br32_1_a_2, br32_1_a[7], out_6}), .Rm(in_2), .LectEcr(undriven), .Rn(in_3));  // open: Clk
  // also tied to GND on the sheet: {br32_1_a[7], br32_1_b[7]}
endmodule
