// Logisim project Controleur.circ as structural Verilog: 2 circuits, main circuit main
module main (
  input  [7:0] in_1,
  input  in_2,
  output [3:0] Opcode,
  output [4:0] Shift,
  output Sel,
  output LoadStore,
  output [4:0] imm5,
  output [3:0] Cond,
  output [2:0] Rm,
  output [2:0] Rn,
  output [2:0] Rd,
  output [7:0] imm8,
  output [2:0] Rt
);

  wire Clock_out;
  wire [7:0] adder_1_out, PC_q;
  wire [15:0] RI_q, rom_1_data;

  ROM #(.dataWidth(16)) rom_1 (.addr(PC_q), .data(rom_1_data));
  Register #(.width(16)) RI (.D(rom_1_data), .en(in_2), .clk(Clock_out), .Q(RI_q));  // open: clr
  Clock Clock (.out(Clock_out));
  Adder adder_1 (.a(PC_q), .b(in_1), .out(adder_1_out));  // open: cin, cout
  Register PC (.D(adder_1_out), .en(in_2), .clk(Clock_out), .Q(PC_q));  // open: clr
  DataProcessing dataprocessing_1 (
    .Cond(Cond), .Shift(Shift), .ULACode(Opcode), .imm5(imm5), .Sel(Sel), .PC(RI_q), .LoadStore(LoadStore),
    .Rm(Rm), .Rn(Rn), .Rd(Rd), .Rt(Rt), .Imm8(imm8));

  // Notes on the sheet:
  //   contents of rom_1 (hex, n*v repeats v):
  //   1 10 11 100 101 110 111 1000 1001 1011 1100 1101 1100 1101 1110 1111
endmodule

module DataProcessing (
  input  [15:0] PC,
  output [3:0] ULACode,
  output [4:0] Shift,
  output Sel,
  output LoadStore,
  output [4:0] imm5,
  output [3:0] Cond,
  output [2:0] Rm,
  output [2:0] Rn,
  output [2:0] Rd,
  output [7:0] Imm8,
  output [2:0] Rt
);

  wire and_3_out, comparator_4_eq, comparator_5_eq, comparator_6_eq, comparator_7_eq, comparator_8_eq,
       comparator_9_eq, comparator_11_eq, comparator_12_eq, comparator_13_eq, ExceptionDataProcessing,
       ExceptionShiftRdImm, ExceptionShiftRmn, isBranch, isDataProcessing, isLS, isMove, isNOP, isShift,
       not_1_out, not_2_out, not_3_out, not_4_out, not_5_out, or_1_out, or_2_out;
  wire [2:0] multiplexer_1_out, multiplexer_2_out, multiplexer_3_out, multiplexer_5_out, multiplexer_6_out;
  wire [5:0] Answer;
  wire [7:0] multiplexer_20_out;

  Comparator #(.width(3)) comparator_1 (.a(ULACode[3:1]), .b(3'b100), .eq(isMove));  // open: gt, lt
  Comparator #(.width(6)) comparator_2 (.a(PC[15:10]), .b(6'b010000), .eq(isDataProcessing));  // open: gt, lt
  Comparator #(.width(2)) comparator_3 (.a(PC[15:14]), .b(2'b00), .eq(isShift));  // open: gt, lt
  Comparator #(.width(3)) comparator_4 (.a(3'b011), .b(PC[15:13]), .eq(comparator_4_eq));  // open: gt, lt
  Comparator #(.width(3)) comparator_5 (.a(PC[15:13]), .b(3'b100), .eq(comparator_5_eq));  // open: gt, lt
  Comparator #(.width(4)) comparator_6 (.a(PC[15:12]), .b(4'b0101), .eq(comparator_6_eq));  // open: gt, lt
  Comparator #(.width(4)) comparator_7 (.a(PC[15:12]), .b(4'b0110), .eq(comparator_7_eq));  // open: gt, lt
  Comparator #(.width(4)) comparator_8 (.a(PC[15:12]), .b(4'b1101), .eq(comparator_8_eq));  // open: gt, lt
  Comparator #(.width(3)) comparator_9 (.a(ULACode[3:1]), .b(3'b111), .eq(comparator_9_eq));  // open: gt, lt
  not not_1 (not_1_out, isShift);
  not not_2 (not_2_out, isLS);
  not not_3 (not_3_out, comparator_9_eq);
  not not_4 (not_4_out, isDataProcessing);
  not not_5 (not_5_out, isBranch);
  and and_1 (ExceptionShiftRdImm, isMove, isShift);
  or or_1 (or_1_out, comparator_4_eq, comparator_5_eq, comparator_6_eq);
  and and_2 (isBranch, comparator_8_eq, not_3_out);
  and and_3 (and_3_out, not_4_out, not_1_out, not_2_out, not_5_out);
  Comparator #(.width(1)) comparator_10 (.a(and_3_out), .b(1'b1), .eq(isNOP));  // open: gt, lt
  Multiplexer #(.width(3), .enable("false")) multiplexer_1 (
    .in0(Answer[5:3]), .in1(Answer[2:0]), .out(multiplexer_1_out), .sel(ExceptionDataProcessing));
  Multiplexer #(.width(3), .enable("false")) multiplexer_2 (
    .in0(Answer[2:0]), .in1(Answer[5:3]), .out(multiplexer_2_out), .sel(ExceptionDataProcessing));
  Multiplexer #(.width(3), .enable("false")) multiplexer_3 (
    .in0(Answer[2:0]), .in1({PC[10], ULACode[3:2]}), .out(multiplexer_3_out), .sel(ExceptionShiftRdImm));
  Multiplexer #(.width(3), .enable("false")) multiplexer_4 (
    .in0(Answer[5:3]), .out(Rm), .sel(ExceptionShiftRdImm));  // open: in1
  and and_4 (isLS, or_1_out, comparator_7_eq);
  Multiplexer #(.width(3), .enable("false")) multiplexer_5 (
    .in1(Answer[4:2]), .out(multiplexer_5_out), .sel(ExceptionShiftRmn));  // open: in0
  Multiplexer #(.width(3), .enable("false")) multiplexer_6 (
    .in1({ULACode[1:0], Answer[5]}), .out(multiplexer_6_out), .sel(ExceptionShiftRmn));  // open: in0
  Multiplexer #(.width(3), .enable("false")) multiplexer_7 (
    .in0(multiplexer_3_out), .out(Rd), .sel(ExceptionShiftRmn));  // open: in1
  Multiplexer #(.width(3), .enable("false")) multiplexer_8 (
    .in0(Answer[2:0]), .out(Rn), .sel(ExceptionShiftRdImm));  // open: in1
  Comparator #(.width(5)) comparator_11 (
    .a(5'b01100), .b({ULACode, Answer[5]}), .eq(comparator_11_eq));  // open: gt, lt
  Comparator #(.width(5)) comparator_12 (
    .a({ULACode, Answer[5]}), .b(5'b01101), .eq(comparator_12_eq));  // open: gt, lt
  Multiplexer #(.width(5), .enable("false")) multiplexer_9 (
    .in0({5{1'b0}}), .in1({ULACode, Answer[5]}), .out(Shift), .sel(isShift));
  Comparator #(.width(3)) comparator_13 (.a({PC[6], PC[7], PC[9]}), .b(3'b101), .eq(comparator_13_eq));  // open: gt, lt
  or or_2 (or_2_out, comparator_11_eq, comparator_12_eq);
  Multiplexer #(.width(3), .enable("false")) multiplexer_10 (
    .in1(multiplexer_1_out), .out(Rm), .sel(isDataProcessing));  // open: in0
  Multiplexer #(.width(3), .enable("false")) multiplexer_11 (
    .in1(multiplexer_2_out), .out(Rn), .sel(isDataProcessing));  // open: in0
  Multiplexer #(.width(3), .enable("false")) multiplexer_12 (
    .in1(Answer[2:0]), .out(Rd), .sel(isDataProcessing));  // open: in0
  Multiplexer #(.width(3), .enable("false")) multiplexer_13 (
    .in1(multiplexer_5_out), .out(Rn), .sel(isShift));  // open: in0
  Multiplexer #(.width(3), .enable("false")) multiplexer_14 (
    .in1(multiplexer_6_out), .out(Rm), .sel(isShift));  // open: in0
  Multiplexer #(.width(3), .enable("false")) multiplexer_15 (.in1(Answer[5:3]), .out(Rn), .sel(isLS));  // open: in0
  Multiplexer #(.width(3), .enable("false")) multiplexer_16 (.in0(3'b000), .in1(Answer[2:0]), .out(Rt), .sel(isLS));
  Multiplexer #(.enable("false")) multiplexer_17 (.in0(1'b0), .in1(1'b1), .out(Sel), .sel(isLS));
  Multiplexer #(.enable("false")) multiplexer_18 (.in0(1'b0), .in1(1'b1), .out(LoadStore), .sel(PC[11]));
  and and_5 (ExceptionDataProcessing, comparator_13_eq, isDataProcessing);
  and and_6 (ExceptionShiftRmn, or_2_out, isShift);
  Multiplexer #(.width(10), .enable("false")) multiplexer_19 (
    .in0(PC[9:0]), .in1({10{1'b0}}), .out({ULACode, Answer}), .sel(isNOP));
  Multiplexer #(.width(8), .enable("false")) multiplexer_20 (
    .in0({8{1'b0}}), .in1({ULACode[1:0], Answer}), .out(multiplexer_20_out), .sel(isBranch));
  Multiplexer #(.width(4), .enable("false")) multiplexer_21 (.in0(4'b0000), .in1(ULACode), .out(Cond), .sel(isBranch));
  Multiplexer #(.width(8), .enable("false")) multiplexer_22 (
    .in0(multiplexer_20_out), .in1({ULACode[1:0], Answer}), .out(Imm8), .sel(ExceptionShiftRdImm));
  Multiplexer #(.width(5), .enable("false")) multiplexer_23 (
    .in0({5{1'b0}}), .in1({PC[10], ULACode}), .out(imm5), .sel(isLS));

  // Other names for the same wires on the sheet: DataCode[9:0] = PC[9:0]; Change[2:0] = {PC[6], PC[7], PC[9]};
  //   Answer[9:6] = ULACode; codeShift[4:0] = {ULACode, Answer[5]}; Conditional[2:0] = ULACode[3:1];
  //   imm5LS[4:0] = {PC[10], ULACode}; Move[2:0] = ULACode[3:1]; RdMove[2:0] = {PC[10], ULACode[3:2]};
  //   ULACodeDefault[3:0] = ULACode; b10 = PC[10]; OpCodeData[5:0] = PC[15:10];
  //   imm8Branch[7:0] = {ULACode[1:0], Answer}; imm8Shift[7:0] = {ULACode[1:0], Answer};
  //   RndDefault[2:0] = Answer[2:0]; checkBL[3:0] = PC[15:12]; opA[3:0] = PC[15:12]; CheckLoad[2:0] = PC[15:13];
  //   CheckShift[1:0] = PC[15:14]; CheckLoadOrStore = PC[11]; RmDefault[2:0] = Answer[5:3];
  //   RmShift[2:0] = {ULACode[1:0], Answer[5]}; RnShift[2:0] = Answer[4:2]

  // Notes on the sheet:
  //   00 binary
  //   100 binary
  //   111 binary
  //   010000 binary
  //   011 binary
  //   100 binary
  //   0101 binary
  //   0110 binary
  //   1101 binary
  //   Set Default of rm rn rd 
  //   2 1 0
  //   Opcode of DataProcessing only if the opcode = 010000
  //   Opcode of Shift only if the opcode = 00xxxx
  //   Opcode of Branch only if the opcode = 1101xx
  //   5 4 3
  //   Opcode of Load only if the opcode = 0101xx or 011xxx or 1000xxx
  //   AddRegister -> 
  //   SubtractRegister ->
  //   Putted a OR because I already know its
  //   Its not a operation available if the opcode its diferent of the shift, data processing, load or conditional branch:
  //   1001
  //   101 binary
  //   01100 binary
  //   01101 binary
  //   its impossible be more than 1 of 4 option at the same time
  //   Exception to change RM and RN when:
  //   ReverseSubtractFrom0 and MultiplyTwoRegisters :
  //   if its not of any exception of shift
  //   if its not of any exception of shift
  //   1101
  //   1 only to Ld/S
  //   1 to load, 0 to store
  //   if its with a not validate opcode, it will:
  //   If 0 = Store; 1 = Load
  //   Cond of branch
  //   set all the other information/bits to 0 (to imply a "error")
  //   Rn e Rm to exception of shift:
  //   Add Register and Substract Register
endmodule
