// Logisim project Controleur.circ as structural Verilog: 3 circuits, main circuit main
module main (
  input  [7:0] in_1,
  input  in_2,
  output [2:0] Rd,
  output [2:0] Rm,
  output [2:0] Rn,
  output [3:0] Opcode,
  output LoadStore,
  output Shift,
  output Sel
);

  wire Clock_out;
  wire [7:0] adder_1_out, PC_q;
  wire [15:0] RI_q, rom_1_data;

  ROM #(.dataWidth(16)) rom_1 (.addr(PC_q), .data(rom_1_data));
  Register #(.width(16)) RI (.D(rom_1_data), .en(in_2), .clk(Clock_out), .Q(RI_q));  // open: clr
  Clock Clock (.out(Clock_out));
  Adder adder_1 (.a(PC_q), .b(in_1), .out(adder_1_out));  // open: cin, cout
  Register PC (.D(adder_1_out), .en(in_2), .clk(Clock_out), .Q(PC_q));  // open: clr
  // DataProcessing dataprocessing_1: pin names not known; wires that end beside it: Rd, Rm, Rn, Opcode, LoadStore, Shift, Sel

  // Notes on the sheet:
  //   contents of rom_1 (hex, n*v repeats v):
  //   1 10 11 100 101 110 111 1000 1001 1011 1100 1101 1100 1101 1110 1111
endmodule

module Controleur (
  input  [5:0] DataProcessing,
  input  [15:0] PC
);

  wire comparator_1_eq, multiplexer_1_out;

  Comparator #(.width(6)) comparator_1 (.a(PC[15:10]), .b(DataProcessing), .eq(comparator_1_eq));  // open: gt, lt
  Multiplexer #(.enable("false")) multiplexer_1 (.out(multiplexer_1_out), .sel(comparator_1_eq));  // open: in0, in1

  // Other names for the same wires on the sheet: OpCode[5:0] = PC[15:10]; b0 = PC[0]; b1 = PC[1]; b2 = PC[2];
  //   b3 = PC[3]; b4 = PC[4]; b5 = PC[5]; b6 = PC[6]; b7 = PC[7]; b8 = PC[8]; b9 = PC[9]
endmodule

module DataProcessing (
  input  [15:0] PC,
  input  [5:0] in_2,
  input  [2:0] in_3,
  input  [4:0] in_4,
  input  [1:0] in_5,
  input  [4:0] in_6,
  input  [2:0] in_7,
  input  [2:0] in_8,
  input  [2:0] in_9,
  input  [3:0] in_10,
  input  [3:0] in_11,
  input  in_12,
  input  [9:0] in_13,
  input  [2:0] in_14,
  output [3:0] ULACode,
  output [4:0] Shift,
  output Sel,
  output LoadStore,
  output [3:0] Cond,
  output [2:0] Rm,
  output [2:0] Rn,
  output [2:0] Rd,
  output [7:0] Imm8,
  output [2:0] Rt
);

  wire and_2_out, comparator_4_eq, comparator_5_eq, comparator_6_eq, comparator_9_eq, comparator_10_eq,
       comparator_11_eq, ExceptionDataProcessing, ExceptionShiftRdImm, ExceptionShiftRmn, isBranch,
       isDataProcessing, isLS, isMove, isNOP, isShift, not_1_out, not_2_out, not_3_out, not_4_out, or_2_out;
  wire [2:0] multiplexer_1_out, multiplexer_2_out, multiplexer_3_out, multiplexer_4_out, multiplexer_6_out;
  wire [5:0] Answer;

  Comparator #(.width(3)) comparator_1 (.a(ULACode[3:1]), .b(in_7), .eq(isMove));  // open: gt, lt
  Comparator #(.width(6)) comparator_2 (.a(PC[15:10]), .b(in_2), .eq(isDataProcessing));  // open: gt, lt
  Comparator #(.width(2)) comparator_3 (.a(PC[15:14]), .b(in_5), .eq(isShift));  // open: gt, lt
  Comparator #(.width(3)) comparator_4 (.a(in_8), .b(PC[15:13]), .eq(comparator_4_eq));  // open: gt, lt
  Comparator #(.width(3)) comparator_5 (.a(PC[15:13]), .b(in_9), .eq(comparator_5_eq));  // open: gt, lt
  Comparator #(.width(4)) comparator_6 (.a(PC[15:12]), .b(in_10), .eq(comparator_6_eq));  // open: gt, lt
  Comparator #(.width(4)) comparator_7 (.a(PC[15:12]), .b(in_11), .eq(isBranch));  // open: gt, lt
  not not_1 (not_1_out, isShift);
  not not_2 (not_2_out, isLS);
  not not_3 (not_3_out, isDataProcessing);
  not not_4 (not_4_out, isBranch);
  and and_1 (ExceptionShiftRdImm, isMove, isShift);
  or or_1 (isLS, comparator_4_eq, comparator_5_eq, comparator_6_eq);
  and and_2 (and_2_out, not_3_out, not_1_out, not_2_out, not_4_out);
  Comparator #(.width(1)) comparator_8 (.a(and_2_out), .b(in_12), .eq(isNOP));  // open: gt, lt
  Multiplexer #(.width(3), .enable("false")) multiplexer_1 (
    .in0(Answer[5:3]), .in1(Answer[2:0]), .out(multiplexer_1_out), .sel(ExceptionDataProcessing));
  Multiplexer #(.width(3), .enable("false")) multiplexer_2 (
    .in0(Answer[2:0]), .in1(Answer[5:3]), .out(multiplexer_2_out), .sel(ExceptionDataProcessing));
  Multiplexer #(.width(3), .enable("false")) multiplexer_3 (
    .in1(Answer[4:2]), .out(multiplexer_3_out), .sel(ExceptionShiftRmn));  // open: in0
  Multiplexer #(.width(3), .enable("false")) multiplexer_4 (
    .in1({ULACode[1:0], Answer[5]}), .out(multiplexer_4_out), .sel(ExceptionShiftRmn));  // open: in0
  Multiplexer #(.width(3), .enable("false")) multiplexer_5 (
    .in0(multiplexer_6_out), .out(Rd), .sel(ExceptionShiftRmn));  // open: in1
  Multiplexer #(.width(3), .enable("false")) multiplexer_6 (
    .in0(Answer[2:0]), .in1({PC[10], ULACode[3:2]}), .out(multiplexer_6_out), .sel(ExceptionShiftRdImm));
  Multiplexer #(.width(8), .enable("false")) multiplexer_7 (
    .in1({ULACode[1:0], Answer}), .out(Imm8), .sel(ExceptionShiftRdImm));  // open: in0
  Comparator #(.width(5)) comparator_9 (.a(in_4), .b({ULACode, Answer[5]}), .eq(comparator_9_eq));  // open: gt, lt
  Comparator #(.width(5)) comparator_10 (.a({ULACode, Answer[5]}), .b(in_6), .eq(comparator_10_eq));  // open: gt, lt
  Multiplexer #(.width(5), .enable("false")) multiplexer_8 (
    .in0({5{1'b0}}), .in1({ULACode, Answer[5]}), .out(Shift), .sel(isShift));
  Comparator #(.width(3)) comparator_11 (.a({PC[6], PC[7], PC[9]}), .b(in_3), .eq(comparator_11_eq));  // open: gt, lt
  or or_2 (or_2_out, comparator_9_eq, comparator_10_eq);
  Multiplexer #(.width(3), .enable("false")) multiplexer_9 (
    .in1(multiplexer_1_out), .out(Rm), .sel(isDataProcessing));  // open: in0
  Multiplexer #(.width(3), .enable("false")) multiplexer_10 (
    .in1(multiplexer_2_out), .out(Rn), .sel(isDataProcessing));  // open: in0
  Multiplexer #(.width(3), .enable("false")) multiplexer_11 (
    .in1(Answer[2:0]), .out(Rd), .sel(isDataProcessing));  // open: in0
  Multiplexer #(.width(3), .enable("false")) multiplexer_12 (
    .in1(multiplexer_3_out), .out(Rn), .sel(isShift));  // open: in0
  Multiplexer #(.width(3), .enable("false")) multiplexer_13 (
    .in1(multiplexer_4_out), .out(Rm), .sel(isShift));  // open: in0
  Multiplexer #(.width(8), .enable("false")) multiplexer_14 (
    .in1({ULACode[1:0], Answer}), .out(Imm8), .sel(isBranch));  // open: in0
  Multiplexer #(.width(3), .enable("false")) multiplexer_15 (.sel(isBranch));  // open: in0, in1, out
  Multiplexer #(.width(3), .enable("false")) multiplexer_16 (.in1(Answer[5:3]), .out(Rn), .sel(isLS));  // open: in0
  Multiplexer #(.width(3), .enable("false")) multiplexer_17 (.in0(in_14), .in1(Answer[2:0]), .out(Rt), .sel(isLS));
  Multiplexer #(.enable("false")) multiplexer_18 (.in0(1'b0), .in1(PC[11]), .out(LoadStore), .sel(isLS));
  and and_3 (ExceptionDataProcessing, comparator_11_eq, isDataProcessing);
  and and_4 (ExceptionShiftRmn, or_2_out, isShift);
  Multiplexer #(.width(4), .enable("false")) multiplexer_19 (.in1(ULACode), .out(Cond), .sel(isBranch));  // open: in0
  Multiplexer #(.width(10), .enable("false")) multiplexer_20 (
    .in0(PC[9:0]), .in1(in_13), .out({ULACode, Answer}), .sel(isNOP));

  assign Sel = 1'b0;

  // Other names for the same wires on the sheet: checkBL[3:0] = PC[15:12]; CheckLoad[2:0] = PC[15:13];
  //   OpCodeData[5:0] = PC[15:10]; CheckShift[1:0] = PC[15:14]; DataCode[9:0] = PC[9:0];
  //   Change[2:0] = {PC[6], PC[7], PC[9]}; Answer[9:6] = ULACode; codeShift[4:0] = {ULACode, Answer[5]};
  //   imm5LS[4:0] = {PC[10], ULACode}; Move[2:0] = ULACode[3:1]; RdMove[2:0] = {PC[10], ULACode[3:2]};
  //   ULACodeDefault[3:0] = ULACode; b10 = PC[10]; imm8Branch[7:0] = {ULACode[1:0], Answer};
  //   imm8Shift[7:0] = {ULACode[1:0], Answer}; RndDefault[2:0] = Answer[2:0]; CheckLoadOrStore = PC[11];
  //   RmDefault[2:0] = Answer[5:3]; RmShift[2:0] = {ULACode[1:0], Answer[5]}; RnShift[2:0] = Answer[4:2]

  // Notes on the sheet:
  //   Set Default of rm rn rd 
  //   Opcode of DataProcessing only if the opcode = 010000
  //   Opcode of Shift only if the opcode = 00xxxx
  //   Opcode of Branch only if the opcode = 1101xx
  //   Opcode of Load only if the opcode = 0101xx or 011xxx or 1000xxx
  //   AddRegister
  //   SubtractRegister
  //   Putted a OR because I already know its
  //   Its not a operation available if the opcode its diferent of the shift, data processing, load or conditional branch:
  //   1001
  //   its impossible be more than 1 of 4 option at the same time
  //   review->
  //   1 to load, 0 to store
  //   Exception to change RM and RN when:
  //   ReverseSubtractFrom0 and MultiplyTwoRegisters :
  //   1101
  //   1 only to Ld/S
  //   Cond of branch
  //   if its with a not validate opcode, it will:
  //   If 0 = Store; 1 = Load
  //   set all the other information/bits to 0 (to imply a "error")
  //   Rn e Rm to exception of shift:
  //   Add Register and Substract Register
endmodule
