// Logisim project FUSION.circ as structural Verilog: 1 circuit, main circuit main
module main (
  input  [7:0] Adresse_Instru,
  output [31:0] Sortie,
  output out_3,
  output [1:0] Flags
);

  wire main_1_p1, main_1_p2, main_1_p3, main_1_p4;

  // Controleur_main main_1: pin names not known; wires that end beside it: main_1_p1, main_1_p2, main_1_p3, main_1_p4
  // RM rm_1: pin names not known; wires that end beside it: Sortie, Flags
endmodule
