// Logisim project test_VHDL.circ as structural Verilog: 1 circuit, main circuit main
module main (
  input  A,
  input  B,
  output Co,
  output S
);

  wire and_1_out, and_2_out, xor_1_out;

  xor xor_1 (xor_1_out, A, B);
  and and_1 (and_1_out, A, B);
  or or_1 (Co, and_1_out, and_2_out);
  buf and_2 (and_2_out, xor_1_out);  // AND_Gate
  buf xor_2 (S, xor_1_out);  // XOR_Gate
endmodule
